// Digital circuit ALU_Control.dig as structural Verilog
module ALU_Control (
  input  [1:0] alu_op,
  input  [5:0] funct,
  output [3:0] AC
);

  wire and_1_out, or_1_out;

  or or_1 (or_1_out, funct[3], funct[0]);
  and and_1 (and_1_out, alu_op[0], funct[1]);
  and and_2 (AC[0], alu_op[0], or_1_out);
  or or_2 (AC[2], alu_op[1], and_1_out);
  or or_3 (AC[1], ~alu_op[0], ~funct[2]);  // Or
  // Pins of 5 and 6 bits meet at funct
  // Pins of 1 and 4 bits meet at {1'b0, AC[2:0]}

  assign AC[3] = 1'b0;

  // Notes on the sheet:
  //   alu_op: ALUOp_1
  //   AC: ALUControl
endmodule
