// Digital circuit Control.dig as structural Verilog
module Control (
  input  [5:0] Op,
  output RgD,
  output AluS,
  output MTR,
  output RW,
  output MR,
  output MW,
  output B,
  output AO_1,
  output AO_0,
  output J,
  output APC
);

  wire and_1_out, and_2_out, and_3_out, and_4_out, and_5_out, and_7_out, and_8_out, or_1_out, or_2_out,
       or_3_out;

  and and_1 (and_1_out, ~Op[5], ~Op[4], Op[3], ~Op[2], ~Op[1], ~Op[0]);  // And
  and and_2 (and_2_out, ~Op[5], ~Op[4], ~Op[3], ~Op[2], ~Op[1], ~Op[0]);  // And
  and and_3 (and_3_out, Op[5], ~Op[4], ~Op[3], ~Op[2], Op[1], Op[0]);  // And
  and and_4 (and_4_out, Op[5], ~Op[4], Op[3], ~Op[2], Op[1], Op[0]);  // And
  and and_5 (and_5_out, ~Op[5], ~Op[4], ~Op[3], Op[2], ~Op[1], ~Op[0]);  // And
  and and_6 (J, ~Op[5], ~Op[4], ~Op[3], ~Op[2], Op[1], ~Op[0]);  // And
  and and_7 (and_7_out, ~Op[5], ~Op[4], ~Op[3], Op[2], ~Op[1], Op[0]);  // And
  and and_8 (and_8_out, Op[5], Op[4], Op[3], Op[2], Op[1], Op[0]);
  not not_1 (APC, and_8_out);
  or or_1 (or_1_out, and_5_out, and_7_out);
  or or_2 (or_2_out, and_3_out, and_1_out, and_4_out);
  or or_3 (or_3_out, and_3_out, and_1_out, and_2_out);
  and and_9 (RgD, ~J, APC, and_2_out);  // And
  and and_10 (AluS, ~J, APC, or_2_out);  // And
  and and_11 (MTR, ~J, APC, and_3_out);  // And
  and and_12 (RW, ~J, APC, or_3_out);  // And
  and and_13 (MR, ~J, APC, and_3_out);  // And
  and and_14 (MW, ~J, APC, and_4_out);  // And
  and and_15 (B, ~J, APC, or_1_out);  // And
  and and_16 (AO_1, ~J, APC, and_2_out);  // And
  and and_17 (AO_0, ~J, APC, or_1_out);  // And

  // Notes on the sheet:
  //   MTR: MemToReg
  //   RW: RegWrite
  //   MR: MemRead
  //   MW: MemWrite
  //   B: Branch
  //   AO_1: ALUOp_1
  //   AO_0: ALUOp_0
  //   J: Jump
  //   APC: AtualPC
  //   I-format
  //   R-format
  //   LW
  //   SW
  //   BEQ
  //   jump
  //   BNE
  //   Exit
  //   RegDst
  //   AluSrc
  //   MemToReg
  //   RegWrite
  //   MemRead
  //   MemWrite
  //   Branch
  //   ALUOp_1
  //   ALUOp_0
endmodule
