// Digital circuit instruction_mem.dig as structural Verilog
module instruction_mem (
  input  [31:0] _32b__ADDR,
  input  _1b__Enable,
  output [31:0] _32b__Out
);

  wire [31:0] div_1_q;

  Div #(.Bits(32)) div_1 (.a(_32b__ADDR), .b(32'h4), .q(div_1_q));  // open: r
  ROM #(.AddrBits(8), .Bits(32)) rom_1 (.A(div_1_q[7:0]), .sel(_1b__Enable), .D(_32b__Out));

  // Notes on the sheet:
  //   contents of rom_1 (hex, n*v repeats v):
  //   201f0001,20090002,200a0003,200b0004,200c0005,200d0006,200e0007
  //   ,200f0008,20100009,2011000a
endmodule
