// Digital circuit memory_24x32.dig as structural Verilog
module memory_24x32 (
  input  [23:0] address,
  input  [31:0] write_data,
  input  mem_write,
  input  clock,
  input  mem_read,
  output [31:0] data
);

  wire [31:0] ramdualport_1_d;

  RAMDualPort #(.AddrBits(24), .Bits(32)) ramdualport_1 (
    .A(address), .Din(write_data), .str(mem_write), .C(clock), .ld(mem_read), .D(ramdualport_1_d));
  Multiplexer #(.Bits(32)) multiplexer_1 (.sel(mem_read), .in_0({32{1'b0}}), .in_1(ramdualport_1_d), .out(data));

  // Notes on the sheet:
  //   address: Endereço a ser acessado
  //   write_data: Dados a serem gravados
  //   mem_write: Mem Write
  //   clock: Clock
  //   mem_read: Mem Read
endmodule
