// Digital circuit PC.dig as structural Verilog
module PC (
  input  clock,
  input  [31:0] write,
  input  reset,
  input  enable,
  output [31:0] address
);

  wire [31:0] multiplexer_1_out;

  Multiplexer #(.Bits(32)) multiplexer_1 (.sel(reset), .in_0(write), .in_1({32{1'b0}}), .out(multiplexer_1_out));
  Register #(.Bits(32)) register_1 (.D(multiplexer_1_out), .C(clock), .en(enable), .Q(address));
endmodule
