// Digital circuit EX-MEM.dig as structural Verilog
module EX_MEM (
  input  [31:0] EX_rtData,
  input  [31:0] EX_result,
  input  [4:0] EX_dstAddr,
  input  clock,
  input  EX_memToReg,
  input  EX_memWrite,
  input  EX_memRead,
  input  EX_regWrite,
  output [31:0] MEM_rtData,
  output [31:0] MEM_result,
  output [4:0] MEM_dstAddr,
  output MEM_memToReg,
  output MEM_memWrite,
  output MEM_memRead,
  output WB_regWrite
);

  wire pulse_1_p;

  pulse pulse_1 (.Clk(clock), .P(pulse_1_p));
  // reg reg_1: pin names not known; wires that end beside it: EX_regWrite, clock, pulse_1_p, WB_regWrite
  // reg reg_2: pin names not known; wires that end beside it: EX_memRead, clock, pulse_1_p, MEM_memRead
  // reg reg_3: pin names not known; wires that end beside it: EX_memWrite, clock, pulse_1_p, MEM_memWrite
  // reg reg_4: pin names not known; wires that end beside it: EX_memToReg, clock, pulse_1_p, MEM_memToReg
  reg32 reg32_1 (.In(EX_result), .Clk(clock), .Clr(pulse_1_p), .Out(MEM_result));
  reg32 reg32_2 (.In(EX_rtData), .Clk(clock), .Clr(pulse_1_p), .Out(MEM_rtData));
  reg5 reg5_1 (.In(EX_dstAddr), .Clk(clock), .Clr(pulse_1_p), .Out(MEM_dstAddr));

  // Notes on the sheet:
  //   EX_rtData: Dado lido do registrador 2
  //   MEM_rtData: Dado lido do registrador 2
  //   EX_result: Dado lido do registrador 1
  //   MEM_result: Dado lido do registrador 1
  //   EX_dstAddr: Sinal extendido
  //   MEM_dstAddr: Sinal extendido
endmodule
