// Digital circuit ID-EX.dig as structural Verilog
module ID_EX (
  input  [31:0] R_2,
  input  [31:0] R_1,
  input  [31:0] S_32,
  input  Clk,
  input  MTR,
  input  MW,
  input  MR,
  input  RgD,
  input  AluS,
  input  [1:0] AO,
  output [31:0] O_R2,
  output [31:0] O_R1,
  output [31:0] Out_S32,
  output [31:0] O_MTR,
  output O_MW,
  output O_MR,
  output [31:0] O_RgD,
  output O_AluS,
  output [1:0] O_AO
);

  wire d_ff_1_q, d_ff_2_q, d_ff_3_q, d_ff_4_q, d_ff_5_q;
  wire [1:0] d_ff_6_q;
  wire [31:0] d_ff_7_q, d_ff_8_q, d_ff_9_q;

  D_FF d_ff_1 (.D(MR), .C(~Clk), .Q(d_ff_1_q));  // open: nQ
  D_FF d_ff_2 (.D(MW), .C(~Clk), .Q(d_ff_2_q));  // open: nQ
  D_FF d_ff_3 (.D(MTR), .C(~Clk), .Q(d_ff_3_q));  // open: nQ
  D_FF d_ff_4 (.D(RgD), .C(~Clk), .Q(d_ff_4_q));  // open: nQ
  D_FF d_ff_5 (.D(AluS), .C(~Clk), .Q(d_ff_5_q));  // open: nQ
  D_FF #(.Bits(2)) d_ff_6 (.D(AO), .C(~Clk), .Q(d_ff_6_q));  // open: nQ
  D_FF #(.Bits(32)) d_ff_7 (.D(R_1), .C(~Clk), .Q(d_ff_7_q));  // open: nQ
  D_FF #(.Bits(32)) d_ff_8 (.D(R_2), .C(~Clk), .Q(d_ff_8_q));  // open: nQ
  D_FF #(.Bits(32)) d_ff_9 (.D(S_32), .C(~Clk), .Q(d_ff_9_q));  // open: nQ
  D_FF d_ff_10 (.D(d_ff_1_q), .C(Clk), .Q(O_MR));  // open: nQ
  D_FF d_ff_11 (.D(d_ff_2_q), .C(Clk), .Q(O_MW));  // open: nQ
  D_FF d_ff_12 (.D(d_ff_3_q), .C(Clk), .Q(O_MTR[0]));  // open: nQ
  D_FF d_ff_13 (.D(d_ff_4_q), .C(Clk), .Q(O_RgD[0]));  // open: nQ
  D_FF d_ff_14 (.D(d_ff_5_q), .C(Clk), .Q(O_AluS));  // open: nQ
  D_FF #(.Bits(2)) d_ff_15 (.D(d_ff_6_q), .C(Clk), .Q(O_AO));  // open: nQ
  D_FF #(.Bits(32)) d_ff_16 (.D(d_ff_7_q), .C(Clk), .Q(O_R1));  // open: nQ
  D_FF #(.Bits(32)) d_ff_17 (.D(d_ff_8_q), .C(Clk), .Q(O_R2));  // open: nQ
  D_FF #(.Bits(32)) d_ff_18 (.D(d_ff_9_q), .C(Clk), .Q(Out_S32));  // open: nQ
  // Pins of 1 and 32 bits meet at O_MTR
  // Pins of 1 and 32 bits meet at O_RgD

  // Notes on the sheet:
  //   R_2: Dado lido do registrador 2
  //   O_R2: Dado lido do registrador 2
  //   R_1: Dado lido do registrador 1
  //   O_R1: Dado lido do registrador 1
  //   S_32: Sinal extendido
  //   Out_S32: Sinal extendido
endmodule
