// Digital circuit ID-EX_part_2.dig as structural Verilog
module ID_EX_part_2 (
  input  Clk,
  input  [4:0] RgD_1,
  input  [4:0] RgD_2,
  output [4:0] O_RgD_1,
  output [4:0] O_RgD_2
);

  wire [4:0] d_ff_1_q, d_ff_2_q;

  D_FF #(.Bits(5)) d_ff_1 (.D(RgD_1), .C(~Clk), .Q(d_ff_1_q));  // open: nQ
  D_FF #(.Bits(5)) d_ff_2 (.D(RgD_2), .C(~Clk), .Q(d_ff_2_q));  // open: nQ
  D_FF #(.Bits(5)) d_ff_3 (.D(d_ff_1_q), .C(Clk), .Q(O_RgD_1));  // open: nQ
  D_FF #(.Bits(5)) d_ff_4 (.D(d_ff_2_q), .C(Clk), .Q(O_RgD_2));  // open: nQ

  // Notes on the sheet:
  //   RgD_1: Dado lido do registrador 2
  //   O_RgD_1: Dado lido do registrador 2
  //   RgD_2: Sinal extendido
  //   O_RgD_2: Sinal extendido
endmodule
