// Digital circuit IF-ID.dig as structural Verilog
module IF_ID (
  input  [31:0] if_instruction,
  input  clock,
  input  [31:0] enable,
  output [31:0] id_instruction
);

  Register #(.Bits(32)) register_1 (.D(if_instruction), .C(clock), .en(enable[0]), .Q(id_instruction));
  // Pins of 1 and 32 bits meet at enable

  // Notes on the sheet:
  //   if_instruction: (32 bits) Instrução
  //   id_instruction: (32 bits) Instrução
  //   enable: (32 bits) Instrução
endmodule
