// Digital circuit MEM-WB.dig as structural Verilog
module MEM_WB (
  input  [31:0] MEM_result,
  input  [31:0] MEM_readData,
  input  [4:0] MEM_dstAddr,
  input  clock,
  input  MEM_memToReg,
  input  MEM_regWrite,
  output [31:0] WB_result,
  output [31:0] WB_readData,
  output [4:0] WB_dstAddr,
  output WB_memToReg,
  output WB_regWrite
);

  wire pulse_1_p;

  pulse pulse_1 (.Clk(clock), .P(pulse_1_p));
  // reg reg_1: pin names not known; wires that end beside it: MEM_regWrite, clock, pulse_1_p, WB_regWrite
  // reg reg_2: pin names not known; wires that end beside it: MEM_memToReg, clock, pulse_1_p, WB_memToReg
  reg32 reg32_1 (.In(MEM_readData), .Clk(clock), .Clr(pulse_1_p), .Out(WB_readData));
  reg32 reg32_2 (.In(MEM_result), .Clk(clock), .Clr(pulse_1_p), .Out(WB_result));
  reg5 reg5_1 (.In(MEM_dstAddr), .Clk(clock), .Clr(pulse_1_p), .Out(WB_dstAddr));

  // Notes on the sheet:
  //   MEM_result: Dado lido do registrador 2
  //   WB_result: Dado lido do registrador 2
  //   MEM_readData: Dado lido da memória
  //   WB_readData: Dado lido do registrador 1
  //   MEM_dstAddr: Sinal extendido
  //   WB_dstAddr: Sinal extendido
endmodule
