// Digital circuit main.dig as structural Verilog
module main (
  input  clock,
  input  pc_reset
);

  wire ALU_Control_p2, ALU_Control_p5, and_1_out, APC, Banco_de_registradores_p1, Banco_de_registradores_p7,
       Banco_de_registradores_p8, branch, ex_mem_1_mem_memread, ex_mem_1_mem_memtoreg, ex_mem_1_mem_memwrite,
       ex_mem_1_wb_regwrite, id_ex_1_p16, id_ex_1_p17, id_ex_1_p18, id_ex_1_p19, id_ex_1_p20, id_ex_1_p21,
       id_ex_1_p22, id_ex_1_p23, ID_stall, if_id_1_p2, jump, mem_wb_1_wb_memtoreg, or_1_out,
       stall_1_if_stall, ULA_p5;
  wire [1:0] FA, FB;
  wire [3:0] div_1_q, div_2_q, div_3_q, div_4_q, div_5_q, div_6_q, div_7_q, div_8_q, div_8_r;
  wire [4:0] ALU_Control_p1, Banco_de_registradores_p5, ex_mem_1_mem_dstaddr, multiplexer_5_out, undriven_2,
       undriven_3;
  wire [5:0] if_id_1_p4;
  wire [8:0] multiplexer_4_out, UC_b;
  wire [15:0] mul_2_mul, mul_4_mul, mul_5_mul, mul_6_mul, mul_7_mul;
  wire [25:0] jump_constant;
  wire [31:0] add_1_s, add_2_s, barrelshifter_1_out, bitextender_1_out, Constant, div_1_r, div_2_r, div_3_r,
       div_4_r, div_5_r, div_6_r, div_7_r, ex_mem_1_mem_rtdata, id_ex_1_p24, Mem_result,
       mem_wb_1_wb_readdata, mem_wb_1_wb_result, \Memória_de_dados_data ,
       \Memória_de_instruções_instruction , mul_1_mul, mul_3_mul, mul_8_mul, multiplexer_1_out,
       multiplexer_2_out, multiplexer_3_out, multiplexer_6_out, multiplexer_7_out, multiplexer_8_out,
       pc_1_address, R31, ULA_p6, undriven, WB;
  wire [31:4] div_1_q_2, div_2_q_2, div_3_q_2, div_4_q_2, div_5_q_2, div_6_q_2, div_7_q_2, div_8_q_2,
       div_8_r_2;
  wire [31:16] mul_2_mul_2, mul_4_mul_2, mul_5_mul_2, mul_6_mul_2, mul_7_mul_2;

  and and_1 (and_1_out, APC, ~ID_stall);  // And
  or or_1 (or_1_out, and_1_out, branch);
  Add #(.Bits(32)) add_1 (.a(pc_1_address), .b(32'h4), .c_i(1'b0), .s(add_1_s));  // open: c_o
  BarrelShifter #(.Bits(32)) barrelshifter_1 (.in(Constant), .shift(6'b000010), .out(barrelshifter_1_out));
  PC pc_1 (.clock(clock), .write(multiplexer_2_out), .reset(pc_reset), .enable(or_1_out), .address(pc_1_address));
  Add #(.Bits(32)) add_2 (.a(add_1_s), .b(barrelshifter_1_out), .c_i(1'b0), .s(add_2_s));  // open: c_o
  Multiplexer #(.Bits(32)) multiplexer_1 (.sel(branch), .in_0(add_1_s), .in_1(add_2_s), .out(multiplexer_1_out));
  Multiplexer #(.Bits(32)) multiplexer_2 (
    .sel(jump), .in_0(multiplexer_1_out), .in_1({pc_1_address[31:28], jump_constant, 2'b00}),
    .out(multiplexer_2_out));
  instruction_mem \Memória_de_instruções  (.address(pc_1_address), .instruction(\Memória_de_instruções_instruction ));
  Multiplexer #(.Bits(32)) multiplexer_3 (
    .sel(stall_1_if_stall), .in_0(\Memória_de_instruções_instruction ), .in_1({32{1'b0}}),
    .out(multiplexer_3_out));
  Seven_Seg_Hex seven_seg_hex_1 (.d(div_1_q), .dp(1'b0));
  Div #(.Bits(32)) div_1 (.a(R31), .b(mul_1_mul), .q({div_1_q_2, div_1_q}), .r(div_1_r));
  // IF_ID if_id_1: pin names not known; wires that end beside it: multiplexer_3_out, if_id_1_p2, clock, {if_id_1_p4, jump_constant}
  Mul #(.Bits(16)) mul_1 (.a(mul_2_mul), .b(16'ha), .mul(mul_1_mul));
  or or_2 (if_id_1_p2, ~ID_stall, stall_1_if_stall);  // Or
  Div #(.Bits(32)) div_2 (.a(div_1_r), .b({mul_2_mul_2, mul_2_mul}), .q({div_2_q_2, div_2_q}), .r(div_2_r));
  Seven_Seg_Hex seven_seg_hex_2 (.d(div_2_q), .dp(1'b0));
  Mul #(.Bits(16)) mul_2 (.a(mul_3_mul[15:0]), .b(16'ha), .mul({mul_2_mul_2, mul_2_mul}));
  Div #(.Bits(32)) div_3 (.a(div_2_r), .b(mul_3_mul), .q({div_3_q_2, div_3_q}), .r(div_3_r));
  Seven_Seg_Hex seven_seg_hex_3 (.d(div_3_q), .dp(1'b0));
  Mul #(.Bits(16)) mul_3 (.a(mul_4_mul), .b(16'ha), .mul(mul_3_mul));
  Control UC (
    .RgD(UC_b[0]), .AluS(UC_b[1]), .MTR(UC_b[2]), .RW(UC_b[3]), .MR(UC_b[4]), .MW(UC_b[5]), .B(UC_b[6]),
    .AO_1(UC_b[7]), .AO_0(UC_b[8]), .J(jump), .APC(APC), .Op(if_id_1_p4));
  // _32x32 Banco_de_registradores: pin names not known; wires that end beside it: Banco_de_registradores_p1, WB, jump_constant[25:21], jump_constant[20:16], Banco_de_registradores_p5, clock, Banco_de_registradores_p7, Banco_de_registradores_p8, R31
  Seven_Seg_Hex seven_seg_hex_4 (.d(div_4_q), .dp(1'b0));
  Div #(.Bits(32)) div_4 (.a(div_3_r), .b({mul_4_mul_2, mul_4_mul}), .q({div_4_q_2, div_4_q}), .r(div_4_r));
  BitExtender #(.inputBits(16), .outputBits(32)) bitextender_1 (.in(jump_constant[15:0]), .out(bitextender_1_out));
  Seven_Seg_Hex seven_seg_hex_5 (.d(R31[19:16]), .dp(1'b0));
  Mul #(.Bits(16)) mul_4 (.a(mul_5_mul), .b(16'ha), .mul({mul_4_mul_2, mul_4_mul}));
  Multiplexer #(.Bits(9)) multiplexer_4 (.sel(ID_stall), .in_0(UC_b), .in_1({9{1'b0}}), .out(multiplexer_4_out));
  Seven_Seg_Hex seven_seg_hex_6 (.d(R31[15:12]), .dp(1'b0));
  Seven_Seg_Hex seven_seg_hex_7 (.d(div_5_q), .dp(1'b0));
  Div #(.Bits(32)) div_5 (.a(div_4_r), .b({mul_5_mul_2, mul_5_mul}), .q({div_5_q_2, div_5_q}), .r(div_5_r));
  Stall stall_1 (
    .IF_ID_rs(jump_constant[25:21]), .IF_ID_rt(jump_constant[20:16]), .ID_EX_memRead(id_ex_1_p18),
    .ID_EX_rt(undriven_3), .branch(branch), .jump(jump), .ID_stall(ID_stall), .IF_stall(stall_1_if_stall));
  Mul #(.Bits(16)) mul_5 (.a(mul_6_mul), .b(16'ha), .mul({mul_5_mul_2, mul_5_mul}));
  Seven_Seg_Hex seven_seg_hex_8 (.d(R31[11:8]), .dp(1'b0));
  Div #(.Bits(32)) div_6 (.a(div_5_r), .b({mul_6_mul_2, mul_6_mul}), .q({div_6_q_2, div_6_q}), .r(div_6_r));
  // ID_EX id_ex_1: pin names not known; wires that end beside it: multiplexer_4_out[3], multiplexer_4_out[2], multiplexer_4_out[4], multiplexer_4_out[5], multiplexer_4_out[6], multiplexer_4_out[0], multiplexer_4_out[1], multiplexer_4_out[8:7], Banco_de_registradores_p7, Banco_de_registradores_p8, bitextender_1_out, jump_constant[25:21], jump_constant[20:16], jump_constant[15:11], jump_constant[5:0], id_ex_1_p16, id_ex_1_p17, id_ex_1_p18, id_ex_1_p19, id_ex_1_p20, id_ex_1_p21, id_ex_1_p22, id_ex_1_p23, id_ex_1_p24
  Seven_Seg_Hex seven_seg_hex_9 (.d(R31[7:4]), .dp(1'b0));
  Seven_Seg_Hex seven_seg_hex_10 (.d(div_6_q), .dp(1'b0));
  Mul #(.Bits(16)) mul_6 (.a(mul_7_mul), .b(16'ha), .mul({mul_6_mul_2, mul_6_mul}));
  Seven_Seg_Hex seven_seg_hex_11 (.d(R31[3:0]), .dp(1'b0));
  Div #(.Bits(32)) div_7 (.a(div_6_r), .b({mul_7_mul_2, mul_7_mul}), .q({div_7_q_2, div_7_q}), .r(div_7_r));
  Seven_Seg_Hex seven_seg_hex_12 (.d(div_7_q), .dp(1'b0));
  Mul #(.Bits(16)) mul_7 (.a(mul_8_mul[15:0]), .b(16'ha), .mul({mul_7_mul_2, mul_7_mul}));
  Seven_Seg_Hex seven_seg_hex_13 (.d(div_8_q), .dp(1'b0));
  Div #(.Bits(32)) div_8 (.a(div_7_r), .b(mul_8_mul), .q({div_8_q_2, div_8_q}), .r({div_8_r_2, div_8_r}));
  Mul #(.Bits(16)) mul_8 (.a(16'h1), .b(16'ha), .mul(mul_8_mul));
  Multiplexer #(.Bits(5)) multiplexer_5 (
    .sel(id_ex_1_p21), .in_0(undriven_3), .in_1(ALU_Control_p1), .out(multiplexer_5_out));
  Seven_Seg_Hex seven_seg_hex_14 (.d(div_8_r), .dp(1'b0));
  Multiplexer #(.Selector_Bits(2), .Bits(32)) multiplexer_6 (
    .sel(FB), .in_0(undriven), .in_1(WB), .in_2(Mem_result), .in_3(Mem_result), .out(multiplexer_6_out));
  // ALU_Control ALU_Control: pin names not known; wires that end beside it: ALU_Control_p1, ALU_Control_p2, id_ex_1_p23, ALU_Control_p2, ALU_Control_p5
  Multiplexer #(.Bits(32)) multiplexer_7 (
    .sel(id_ex_1_p22), .in_0(multiplexer_6_out), .in_1(Constant), .out(multiplexer_7_out));
  Multiplexer #(.Selector_Bits(2), .Bits(32)) multiplexer_8 (
    .sel(FA), .in_0(id_ex_1_p24), .in_1(WB), .in_2(Mem_result), .in_3(Mem_result), .out(multiplexer_8_out));
  // ula ULA: pin names not known; wires that end beside it: ALU_Control_p5, multiplexer_8_out, multiplexer_7_out, {6{1'b0}}, ULA_p5, ULA_p6
  forwarding_unit Unidade_de_forwarding (
    .RS(undriven_2), .RT(undriven_3), .EX_MEM_dest(ex_mem_1_mem_dstaddr),
    .MEM_WB_dest(Banco_de_registradores_p5), .EX_MEM_rw(ex_mem_1_wb_regwrite),
    .MEM_WB_rw(Banco_de_registradores_p1), .FA(FA), .FB(FB));
  and and_2 (branch, id_ex_1_p20, ULA_p5);
  EX_MEM ex_mem_1 (
    .EX_regWrite(id_ex_1_p16), .EX_memRead(id_ex_1_p18), .EX_memWrite(id_ex_1_p19),
    .EX_memToReg(id_ex_1_p17), .EX_result(ULA_p6), .EX_rtData(multiplexer_6_out),
    .EX_dstAddr(multiplexer_5_out), .clock(clock), .WB_regWrite(ex_mem_1_wb_regwrite),
    .MEM_memRead(ex_mem_1_mem_memread), .MEM_memWrite(ex_mem_1_mem_memwrite),
    .MEM_memToReg(ex_mem_1_mem_memtoreg), .MEM_result(Mem_result), .MEM_rtData(ex_mem_1_mem_rtdata),
    .MEM_dstAddr(ex_mem_1_mem_dstaddr));
  memory_24x32 \Memória_de_dados  (
    .address(Mem_result[23:0]), .write_data(ex_mem_1_mem_rtdata), .mem_write(ex_mem_1_mem_memwrite),
    .mem_read(ex_mem_1_mem_memread), .clock(clock), .data(\Memória_de_dados_data ));
  MEM_WB mem_wb_1 (
    .MEM_regWrite(ex_mem_1_wb_regwrite), .MEM_memToReg(ex_mem_1_mem_memtoreg),
    .MEM_readData(\Memória_de_dados_data ), .MEM_result(Mem_result), .MEM_dstAddr(ex_mem_1_mem_dstaddr),
    .clock(clock), .WB_regWrite(Banco_de_registradores_p1), .WB_memToReg(mem_wb_1_wb_memtoreg),
    .WB_readData(mem_wb_1_wb_readdata), .WB_result(mem_wb_1_wb_result), .WB_dstAddr(Banco_de_registradores_p5));
  Multiplexer #(.Bits(32)) multiplexer_9 (
    .sel(mem_wb_1_wb_memtoreg), .in_0(mem_wb_1_wb_result), .in_1(mem_wb_1_wb_readdata), .out(WB));

  // Notes on the sheet:
  //   clock: Hz: 20
  //   addi $t0, $zero, 1
  //   addi $t1, $zero, 40
  //   sw $t0, 0($zero)
  //   sw $t0, 4($zero)
  //   addi $t2, $zero, 8
  //   for:
  //   beq $t2, $t1, fim
  //   lw $t3, -4($t2)
  //   lw $t4, -8($t2)
  //   add $ra, $t3, $t4
  //   sw $ra, 0($t2)
  //   addi $t2, $t2, 4
  //   j for	
  //   fim:
  //   Reg Destino
  //   MEM/WB_Dest
  //   MEM/WB_RegWrite
endmodule
